// Logisim project F1.circ as structural Verilog: 3 circuits, main circuit main
module main (
  input  A,
  input  B,
  input  A_2,
  input  B_2
);

  wire xnor_1_out_3, xor_1_out_3;

  XOR xor_1 (.in_1(A), .in_2(B), .out_3(xor_1_out_3));
  XNOR xnor_1 (.in_1(A_2), .in_2(B_2), .out_3(xnor_1_out_3));
  LED led_1 (.in(xor_1_out_3));
  LED led_2 (.in(xnor_1_out_3));

  // Notes on the sheet:
  //   F
  //   F
endmodule

module XOR (
  input  in_1,
  input  in_2,
  output out_3
);

  wire nand_1_out, nand_2_out, nand_3_out;

  nand nand_1 (nand_1_out, in_1, in_2);
  nand nand_2 (nand_2_out, in_1, nand_1_out);
  nand nand_3 (nand_3_out, nand_1_out, in_2);
  nand nand_4 (out_3, nand_2_out, nand_3_out);
endmodule

module XNOR (
  input  in_1,
  input  in_2,
  output out_3
);

  wire nand_1_out, nand_2_out, nand_3_out, nand_4_out;

  nand nand_1 (nand_1_out, in_1, in_2);
  nand nand_2 (nand_2_out, in_1, nand_1_out);
  nand nand_3 (nand_3_out, nand_1_out, in_2);
  nand nand_4 (nand_4_out, nand_2_out, nand_3_out);
  nand nand_5 (out_3, nand_4_out, nand_4_out);
endmodule
