// Logisim project F2.circ as structural Verilog: 6 circuits, main circuit main
module main (
  input  A,
  input  A_2,
  input  B,
  input  A_3,
  input  B_2,
  input  A_4,
  input  B_3,
  input  A_5,
  input  B_4
);

  wire and_1_out_3, not_1_out_2, or_1_out_3, xnor_1_out_3, xor_1_out_3;

  NOT not_1 (.in_1(A), .out_2(not_1_out_2));
  AND and_1 (.in_2(B), .in_1(A_2), .out_3(and_1_out_3));
  OR or_1 (.in_1(A_3), .in_2(B_2), .out_3(or_1_out_3));
  XOR xor_1 (.in_1(A_4), .in_2(B_3), .out_3(xor_1_out_3));
  XNOR xnor_1 (.in_1(A_5), .in_2(B_4), .out_3(xnor_1_out_3));
  LED led_1 (.in(not_1_out_2));
  LED led_2 (.in(and_1_out_3));
  LED led_3 (.in(or_1_out_3));
  LED led_4 (.in(xor_1_out_3));
  LED led_5 (.in(xnor_1_out_3));

  // Notes on the sheet:
  //   F
  //   F
  //   F
  //   F
  //   F
endmodule

module NOT (
  input  in_1,
  output out_2
);

  nor nor_1 (out_2, in_1, in_1);
endmodule

module AND (
  input  in_1,
  input  in_2,
  output out_3
);

  wire nor_1_out, nor_2_out;

  nor nor_1 (nor_1_out, in_1, in_1);
  nor nor_2 (nor_2_out, in_2, in_2);
  nor nor_3 (out_3, nor_1_out, nor_2_out);
endmodule

module OR (
  input  in_1,
  input  in_2,
  output out_3
);

  wire nor_1_out;

  nor nor_1 (nor_1_out, in_1, in_2);
  nor nor_2 (out_3, nor_1_out, nor_1_out);
endmodule

module XOR (
  input  in_1,
  input  in_2,
  output out_3
);

  wire nor_1_out, nor_2_out, nor_3_out, nor_4_out;

  nor nor_1 (nor_1_out, in_1, in_1);
  nor nor_2 (nor_2_out, in_2, in_2);
  nor nor_3 (nor_3_out, nor_1_out, nor_2_out);
  nor nor_4 (nor_4_out, in_1, in_2);
  nor nor_5 (out_3, nor_3_out, nor_4_out);
endmodule

module XNOR (
  input  in_1,
  input  in_2,
  output out_3
);

  wire nor_1_out, nor_2_out, nor_3_out;

  nor nor_1 (nor_1_out, in_1, in_2);
  nor nor_2 (nor_2_out, in_1, nor_1_out);
  nor nor_3 (nor_3_out, nor_1_out, in_2);
  nor nor_4 (out_3, nor_2_out, nor_3_out);
endmodule
