// Logisim project F3.circ as structural Verilog: 4 circuits, main circuit main
module main (
  input  A,
  input  B,
  input  C,
  input  A_2,
  input  B_2,
  input  C_2
);

  wire part_1_1_f, part_2_1_f;

  Part_1 part_1_1 (.F(part_1_1_f), .A(A), .B(B), .C(C));
  Part_2 part_2_1 (.F(part_2_1_f), .A(A_2), .B(B_2), .C(C_2));
  LED led_1 (.in(part_1_1_f));
  LED led_2 (.in(part_2_1_f));

  // Notes on the sheet:
  //   F
  //   F
endmodule

module IC7400__NAND (
  input  in_1,
  input  in_2,
  input  in_3,
  input  in_4,
  input  in_5,
  input  in_6,
  input  in_7,
  input  in_8,
  input  in_9,
  input  in_10,
  output out_11,
  output out_12,
  output out_13,
  output out_14
);

  nand nand_1 (out_11, in_1, in_2);
  nand nand_2 (out_12, in_3, in_4);
  nand nand_3 (out_13, in_7, in_8);
  nand nand_4 (out_14, in_9, in_10);
endmodule

module Part_1 (
  input  A,
  input  B,
  input  C,
  output F
);

  wire ic7400_nand_1_out_11, ic7400_nand_1_out_12, ic7400_nand_1_out_13, ic7400_nand_2_out_11,
       ic7400_nand_2_out_12, ic7400_nand_2_out_13, ic7400_nand_2_out_14;

  IC7400__NAND ic7400_nand_1 (
    .in_1(ic7400_nand_1_out_12), .in_2(ic7400_nand_1_out_12), .in_3(A), .in_4(C),
    .in_7(ic7400_nand_1_out_11), .in_8(ic7400_nand_1_out_11), .in_9(ic7400_nand_1_out_13),
    .in_10(ic7400_nand_2_out_14), .out_11(ic7400_nand_1_out_11), .out_12(ic7400_nand_1_out_12),
    .out_13(ic7400_nand_1_out_13), .out_14(F));  // open: in_5, in_6
  IC7400__NAND ic7400_nand_2 (
    .in_1(B), .in_2(ic7400_nand_2_out_12), .in_3(C), .in_4(C), .in_7(ic7400_nand_2_out_11),
    .in_8(ic7400_nand_2_out_11), .in_9(ic7400_nand_2_out_13), .in_10(ic7400_nand_2_out_13),
    .out_11(ic7400_nand_2_out_11), .out_12(ic7400_nand_2_out_12), .out_13(ic7400_nand_2_out_13),
    .out_14(ic7400_nand_2_out_14));  // open: in_5, in_6
endmodule

module Part_2 (
  input  A,
  input  B,
  input  C,
  output F
);

  wire ic7400_nand_1_out_11, ic7400_nand_1_out_12, ic7400_nand_1_out_14;

  IC7400__NAND ic7400_nand_1 (
    .in_1(A), .in_2(C), .in_3(C), .in_4(C), .in_7(ic7400_nand_1_out_11), .in_8(ic7400_nand_1_out_14),
    .in_9(B), .in_10(ic7400_nand_1_out_12), .out_11(ic7400_nand_1_out_11), .out_12(ic7400_nand_1_out_12),
    .out_13(F), .out_14(ic7400_nand_1_out_14));  // open: in_5, in_6
endmodule
