// Logisim project Power Plant Cooling System.circ as structural Verilog: 2 circuits, main circuit main
module main (
  input  S1,
  input  S2,
  input  F1,
  input  F2,
  output A
);

  wire ic7402_nor_1_out_11, ic7402_nor_1_out_12, ic7402_nor_1_out_13;

  IC7402__NOR ic7402_nor_1 (
    .in_1(F1), .in_2(F2), .in_3(ic7402_nor_1_out_11), .in_4(ic7402_nor_1_out_11), .in_7(S2), .in_8(S1),
    .in_9(ic7402_nor_1_out_13), .in_10(ic7402_nor_1_out_12), .out_11(ic7402_nor_1_out_11),
    .out_12(ic7402_nor_1_out_12), .out_13(ic7402_nor_1_out_13), .out_14(A));  // open: in_5, in_6
endmodule

module IC7402__NOR (
  input  in_1,
  input  in_2,
  input  in_3,
  input  in_4,
  input  in_5,
  input  in_6,
  input  in_7,
  input  in_8,
  input  in_9,
  input  in_10,
  output out_11,
  output out_12,
  output out_13,
  output out_14
);

  nor nor_1 (out_11, in_1, in_2);
  nor nor_2 (out_12, in_3, in_4);
  nor nor_3 (out_13, in_7, in_8);
  nor nor_4 (out_14, in_9, in_10);
endmodule
